// Logisim project TP.circ as structural Verilog: 2 circuits, main circuit main
module main (
  input  in_1,
  input  in_2,
  input  [31:0] in_3
);

  wire banc_reg_1_p2, banc_reg_1_p7, decodeur_1_imm_reg;
  wire [1:0] decodeur_1_op;
  wire [3:0] decodeur_1_rd, decodeur_1_rs1, decodeur_1_rs2;
  wire [31:0] banc_reg_1_p8, multiplexer_1_out;

  decodeur decodeur_1 (
    .Rd(decodeur_1_rd), .Rs1(decodeur_1_rs1), .Rs2(decodeur_1_rs2), .Op(decodeur_1_op),
    .Imm_reg(decodeur_1_imm_reg));  // open: in_1, Imm, Rot
  // banc_reg banc_reg_1: pin names not known; wires that end beside it: in_1, banc_reg_1_p2, decodeur_1_rs1, decodeur_1_rs2, decodeur_1_rd, in_2, banc_reg_1_p7, banc_reg_1_p8
  // Probe on banc_reg_1_p8
  Multiplexer #(.width(32)) multiplexer_1 (
    .in0(banc_reg_1_p8), .in1(in_3), .out(multiplexer_1_out), .sel(decodeur_1_imm_reg));
  // ALU alu_1: pin names not known; wires that end beside it: banc_reg_1_p7, multiplexer_1_out, decodeur_1_op, banc_reg_1_p2
endmodule

module decodeur (
  input  [31:0] in_1,
  output [3:0] Rd,
  output [3:0] Rs1,
  output [3:0] Rs2,
  output [1:0] Op,
  output Imm_reg,
  output [7:0] Imm,
  output [3:0] Rot
);

  wire and_1_out, not_1_out;

  not not_1 (not_1_out, in_1[24]);
  and and_1 (and_1_out, in_1[23], not_1_out);
  or or_1 (Op[0], in_1[21], in_1[22]);
  or or_2 (Op[1], in_1[22], and_1_out);

  assign Imm_reg = in_1[25];
  assign Rd = in_1[15:12];
  assign Rs1 = in_1[19:16];
endmodule
